// Logisim project regfile.circ as structural Verilog
module register_file (
  input  [15:0] write_data,
  input  [2:0] rs,
  input  [2:0] rd,
  input  [2:0] rt,
  output [15:0] read_data1,
  output [15:0] read_data2
);

  wire clock_1_out, decoder_1_out0, decoder_1_out1, decoder_1_out2, decoder_1_out3, decoder_1_out4,
       decoder_1_out5, decoder_1_out6, decoder_1_out7;
  wire [15:0] R0_q, R1_q, R2_q, R3_q, R4_q, R5_q, R6_q, R7_q;

  Decoder #(.select(3)) decoder_1 (
    .out0(decoder_1_out0), .out1(decoder_1_out1), .out2(decoder_1_out2), .out3(decoder_1_out3),
    .out4(decoder_1_out4), .out5(decoder_1_out5), .out6(decoder_1_out6), .out7(decoder_1_out7), .sel(rd),
    .en(1'b1));
  Clock clock_1 (.out(clock_1_out));
  Register #(.width(16)) R0 (.D(write_data), .en(decoder_1_out0), .clk(clock_1_out), .Q(R0_q));  // open: clr
  Register #(.width(16)) R1 (.D(write_data), .en(decoder_1_out1), .clk(clock_1_out), .Q(R1_q));  // open: clr
  Register #(.width(16)) R2 (.D(write_data), .en(decoder_1_out2), .clk(clock_1_out), .Q(R2_q));  // open: clr
  Register #(.width(16)) R3 (.D(write_data), .en(decoder_1_out3), .clk(clock_1_out), .Q(R3_q));  // open: clr
  Register #(.width(16)) R4 (.D(write_data), .en(decoder_1_out4), .clk(clock_1_out), .Q(R4_q));  // open: clr
  Register #(.width(16)) R5 (.D(write_data), .en(decoder_1_out5), .clk(clock_1_out), .Q(R5_q));  // open: clr
  Register #(.width(16)) R6 (.D(write_data), .en(decoder_1_out6), .clk(clock_1_out), .Q(R6_q));  // open: clr
  Register #(.width(16)) R7 (.D(write_data), .en(decoder_1_out7), .clk(clock_1_out), .Q(R7_q));  // open: clr
  Multiplexer #(.select(3), .width(16)) multiplexer_1 (
    .in0(R0_q), .in1(R1_q), .in2(R2_q), .in3(R3_q), .in4(R4_q), .in5(R5_q), .in6(R6_q), .in7(R7_q),
    .out(read_data1), .sel(rs));
  Multiplexer #(.select(3), .width(16)) multiplexer_2 (
    .in0(R0_q), .in1(R1_q), .in2(R2_q), .in3(R3_q), .in4(R4_q), .in5(R5_q), .in6(R6_q), .in7(R7_q),
    .out(read_data2), .sel(rt));
endmodule
